# Fritzing sketch multiplexer_circuit (saved by Fritzing 0.9.3b)
breadboards: 5

parts:
  Part1 = Arduino Uno (Rev3) - ICSP
  U1 = MIDI_CONN_FEMALE [package=din_5_female]
  R1 = Resistor [tolerance=±5% resistance=220 package=THT]
  R2 = Resistor [tolerance=±5% resistance=220 package=THT]
  J2 = Piezo Speaker
  R6 = Resistor [tolerance=±5% resistance=1M package=THT]
  R7 = Resistor [tolerance=±5% resistance=1M package=THT]
  R8 = Resistor [tolerance=±5% resistance=1M package=THT]
  C3 = Ceramic Capacitor [capacitance=1µF voltage=50V package="200 mil [THT, multilayer]"]
  C4 = Ceramic Capacitor [capacitance=1µF voltage=50V package="200 mil [THT, multilayer]"]
  R9 = Resistor [tolerance=±5% resistance=10k package=THT]
  D3 = Rectifier Diode [part_number=1N4001 package="300 mil [THT]"]
  J3 = Piezo Speaker
  R10 = Resistor [tolerance=±5% resistance=1M package=THT]
  R11 = Resistor [tolerance=±5% resistance=1M package=THT]
  R12 = Resistor [tolerance=±5% resistance=10k package=THT]
  R13 = Resistor [tolerance=±5% resistance=1M package=THT]
  D4 = Rectifier Diode [part_number=1N4001 package="300 mil [THT]"]
  C5 = Ceramic Capacitor [capacitance=1µF voltage=50V package="200 mil [THT, multilayer]"]
  C6 = Ceramic Capacitor [capacitance=1µF voltage=50V package="200 mil [THT, multilayer]"]
  U2 = 74HC4052 [package=dil16]

nets:
  N1: Part1.A0, U2.X
  N2: Part1.D8, U2.B
  GND: Part1.GND, U1.NC1, J2.pin1, R8.Pin_1, C3.0, C4.1, R9.Pin_1, J3.pin1, R10.Pin_1, R12.Pin_1, C5.0, C6.1, U2.VEE, U2.GND
  N3: Part1.D1/TX, R1.Pin_1
  N4: Part1.D7, U2.A
  5V: Part1.5V, R2.Pin_1, U2.VCC
  N5: U1.MIDI_IN, R1.Pin_0
  N6: U1.MIDI_OUT, R2.Pin_0
  N7: J2.pin2, R6.Pin_0, D3.anode
  N8: R6.Pin_1, R7.Pin_0
  N9: R7.Pin_1, R8.Pin_0
  N10: C3.1, C4.0, R9.Pin_0, D3.cathode, U2.X1
  N11: J3.pin2, R11.Pin_0, D4.anode
  N12: R10.Pin_0, R13.Pin_1
  N13: R11.Pin_1, R13.Pin_0
  N14: R12.Pin_0, D4.cathode, C5.1, C6.0, U2.X0
