# Fritzing sketch single_sensor (saved by Fritzing 0.9.3b)
breadboards: 1

parts:
  Part1 = Arduino Uno (Rev3) - ICSP
  U1 = MIDI_CONN_FEMALE [package=din_5_female]
  R1 = Resistor [tolerance=±5% resistance=220 package=THT]
  R2 = Resistor [tolerance=±5% resistance=220 package=THT]
  J1 = Piezo Speaker
  R3 = Resistor [tolerance=±5% resistance=1M package=THT]
  R4 = Resistor [tolerance=±5% resistance=1M package=THT]
  R5 = Resistor [tolerance=±5% resistance=1M package=THT]
  D1 = Rectifier Diode [part_number=1N4001 package="300 mil [THT]"]
  C1 = Ceramic Capacitor [capacitance=1µF voltage=50V package="100 mil [THT, multilayer]"]  # not connected
  C2 = Ceramic Capacitor [capacitance=1µF package="200 mil [THT, multilayer]"]
  C2_2 = Ceramic Capacitor [capacitance=1µF voltage=50V package="200 mil [THT, multilayer]"]
  R6 = Resistor [tolerance=±5% resistance=10k package="0603 [SMD]"]

nets:
  N1: Part1.A0, D1.cathode, C2.0, C2_2.0, R6.Pin_0
  N2: Part1.GND, U1.NC1, J1.pin1, R5.Pin_0, C2.1, C2_2.1, R6.Pin_1
  N3: Part1.5V, R2.Pin_1
  N4: U1.MIDI_IN, R1.Pin_0
  N5: U1.MIDI_OUT, R2.Pin_0
  N6: J1.pin2, R3.Pin_1, D1.anode
  N7: R3.Pin_0, R4.Pin_1
  N8: R4.Pin_0, R5.Pin_1
